// Digital circuit ALU.dig as structural Verilog
module ALU (
  input  S3,
  input  S2,
  input  S4,
  input  [7:0] A,
  input  [7:0] B,
  input  S1,
  output [7:0] out,
  output ovf
);

  wire and_1_out, and_2_out, and_3_out, not_1_out, not_2_out, not_3_out, Over1, Over2, Over3, Over4, Over5,
       S1_t, S2_t, S3_t, S4_t, S5, S6, S7, S8;
  wire [7:0] O1, O2, O3, O4, O5, O6, O7, O8, O9;

  not not_1 (not_1_out, S1);
  not not_2 (not_2_out, S1);
  not not_3 (not_3_out, S1);
  and and_1 (and_1_out, not_1_out, S4);
  and and_2 (and_2_out, not_2_out, S2);
  and and_3 (and_3_out, not_3_out, S3);
  // seletor seletor_1: pin names not known; wires that end beside it: and_1_out, and_2_out, and_3_out, S1_t, S2_t, S3_t, S4_t, S5, S6, S7, S8
  // multiplicador_4_bits_ativador multiplicador_4_bits_ativador_1: pin names not known; wires that end beside it: S1_t, A, B, O1, Over1
  // subtrator_8_bits_ativador subtrator_8_bits_ativador_1: pin names not known; wires that end beside it: S2_t, A, B, Over2, O2
  // right_shift right_shift_1: pin names not known; wires that end beside it: S3_t, A, Over3, O3
  // AND_ativador and_ativador_1: pin names not known; wires that end beside it: A, B, S4_t, O4
  // carregador carregador_1: pin names not known; wires that end beside it: A, S1, O9
  // somador_8_bits_ativador somador_8_bits_ativador_1: pin names not known; wires that end beside it: S5, A, B, Over4, O5
  // shift_left shift_left_1: pin names not known; wires that end beside it: S6, A, Over5, O6
  // OR_ativador or_ativador_1: pin names not known; wires that end beside it: A, B, S7, O7
  // XOR_ativador xor_ativador_1: pin names not known; wires that end beside it: A, B, S8, O8
  assign out = O1 | O2 | O3 | O4 | O9 | O5 | O6 | O7 | O8;  // Or or_1, 8 bits wide
  or or_2 (ovf, Over1, Over2, Over3, Over4, Over5);

  // Other names for the same wires on the sheet: Carregar = S1; O[7:0] = out; Overflow = ovf
endmodule
