// Digital circuit CPU.dig as structural Verilog
module CPU (
  input  clk,
  input  [3:0] \Endereço ,
  input  [11:0] Palavra_de_Instrucao
);

  wire Overflow, S1, S2, S3, S4;
  wire [7:0] A, B, O;

  EEPROMDualPort #(.AddrBits(4), .Bits(12)) eepromdualport_1 (
    .A(\Endereço ), .Din({12{1'b0}}), .str(1'b0), .C(clk), .ld(1'b1), .D({S1, S2, S3, S4, A}));
  Register #(.Bits(8)) Acumulador (.D(O), .C(clk), .en(1'b1), .Q(B));
  ALU alu_1 (.S3(S3), .S2(S2), .S4(S4), .A(A), .B(B), .S1(S1), .out(O), .ovf(Overflow));
  Seven_Seg_Hex seven_seg_hex_1 (.d(B[7:4]), .dp(1'b0));
  LED led_1 (.in(Overflow));
  Seven_Seg_Hex seven_seg_hex_2 (.d(B[3:0]), .dp(1'b0));

  // Other names for the same wires on the sheet: Clock = clk; Endereco[3:0] = \Endereço ;
  //   PalavraInstrucao[11:0] = Palavra_de_Instrucao

  // Notes on the sheet:
  //   Instruçoes
  //   Bit mais significativo
  //   1 => carregar operando no acumulador
  //   0 => realizar operaçao dos proximos 3 bits
  //   Proximos 3 bits:
  //   000 => multiplicar
  //   001 =>
  //   010 =>
  //   011 =>
  //   100 =>
  //   101 =>
  //   110 =>
  //   111 =>
  //   Demais bits: operando
  //   contents of eepromdualport_1 (hex, n*v repeats v):
  //   174876e801,2,1000001,6*0,3e8
endmodule
